// Logisim project alu.circ as structural Verilog: 1 circuit, main circuit alu
module alu (
  input  [31:0] A,
  input  [31:0] B,
  input  [3:0] ALUSel,
  output [31:0] Result
);

  wire comparator_1_lt, comparator_2_eq, comparator_3_eq, comparator_4_eq, or_2_out, xor_1_out;
  wire [4:0] bit_extender_1_out, bit_extender_2_out, bit_extender_4_out;
  wire [6:0] bitadder_1_out;
  wire [31:0] add, and1, bitpal, cnto, divu, mulh, mult, multiplexer_1_out, multiplexer_2_out,
       multiplier_1_cout, multiplier_1_out, negator_1_out, negator_2_out, negator_3_out, negator_4_out, or1,
       remu, sir, sll1, slt, sra1, srl1, sub, subtractor_2_out, xor1;

  Multiplexer #(.width(32), .enable("false")) multiplexer_1 (
    .in0(A), .in1(negator_1_out), .out(multiplexer_1_out), .sel(A[31]));
  Negator #(.width(32)) negator_1 (.in(A), .out(negator_1_out));
  Multiplexer #(.width(32), .enable("false")) multiplexer_2 (
    .in0(B), .in1(negator_2_out), .out(multiplexer_2_out), .sel(B[31]));
  Negator #(.width(32)) negator_2 (.in(B), .out(negator_2_out));
  Adder #(.width(32)) adder_1 (.a(A), .b(B), .out(add));  // open: cin, cout
  Subtractor #(.width(32)) subtractor_1 (.a(A), .b(B), .out(sub));  // open: bin, bout
  Multiplier #(.width(32)) multiplier_1 (
    .a(multiplexer_1_out), .b(multiplexer_2_out), .out(multiplier_1_out), .cout(multiplier_1_cout));  // open: cin
  Negator #(.width(32)) negator_3 (.in(multiplier_1_cout), .out(negator_3_out));
  xor xor_1 (xor_1_out, A[31], B[31]);
  Negator #(.width(32)) negator_4 (.in(multiplier_1_out), .out(negator_4_out));
  Subtractor #(.width(32)) subtractor_2 (.a(negator_3_out), .b(32'h1), .out(subtractor_2_out));  // open: bin, bout
  Multiplexer #(.width(32), .enable("false")) multiplexer_3 (
    .in0(multiplier_1_out), .in1(negator_4_out), .out(mult), .sel(xor_1_out));
  Multiplexer #(.width(32), .enable("false")) multiplexer_4 (
    .in0(multiplier_1_cout), .in1(subtractor_2_out), .out(mulh), .sel(xor_1_out));
  Divider #(.width(32)) divider_1 (.a(A), .b(B), .out(divu), .rem(remu));  // open: upper
  assign and1 = A & B;  // AND_Gate and_1, 32 bits wide
  assign or1 = A | B;  // OR_Gate or_1, 32 bits wide
  assign xor1 = A ^ B;  // XOR_Gate xor_2, 32 bits wide
  Bit_Extender #(.in_width(32), .out_width(5)) bit_extender_1 (.in(B), .out(bit_extender_1_out));
  Comparator #(.width(32)) comparator_1 (.a(A), .b(B), .lt(comparator_1_lt));  // open: gt, eq
  Bit_Extender #(.in_width(32), .out_width(5)) bit_extender_2 (.in(B), .out(bit_extender_2_out));
  Multiplexer #(.select(4), .width(32), .enable("false")) multiplexer_5 (
    .in0(add), .in1(sub), .in2(mulh), .in3(mult), .in4(divu), .in5(remu), .in6(and1), .in7(or1), .in8(xor1),
    .in9(sll1), .in10(slt), .in11(sra1), .in12(srl1), .in13(cnto), .in14(bitpal), .in15(sir), .out(Result),
    .sel(ALUSel));
  Shifter #(.width(32)) shifter_1 (.in(A), .\dist (bit_extender_1_out), .out(sll1));
  assign slt = {{31{1'b0}}, comparator_1_lt};  // Bit_Extender bit_extender_3
  Shifter #(.width(32), .shift("ar")) shifter_2 (.in(A), .\dist (bit_extender_2_out), .out(sra1));
  Bit_Extender #(.in_width(32), .out_width(5)) bit_extender_4 (.in(B), .out(bit_extender_4_out));
  BitAdder #(.width(32)) bitadder_1 (.in0(A), .in1(B), .out(bitadder_1_out));
  Shifter #(.width(32), .shift("lr")) shifter_3 (.in(A), .\dist (bit_extender_4_out), .out(srl1));
  assign cnto = {{25{1'b0}}, bitadder_1_out};  // Bit_Extender bit_extender_5
  Comparator #(.width(16)) comparator_2 (
    .a(A[15:0]),
    .b({A[16], A[17], A[18], A[19], A[20], A[21], A[22], A[23], A[24], A[25], A[26], A[27], A[28], A[29], A[30], A[31]}),
    .eq(comparator_2_eq));  // open: gt, lt
  or or_2 (or_2_out, comparator_2_eq, comparator_3_eq);
  Comparator #(.width(16)) comparator_3 (
    .a(B[15:0]),
    .b({B[16], B[17], B[18], B[19], B[20], B[21], B[22], B[23], B[24], B[25], B[26], B[27], B[28], B[29], B[30], B[31]}),
    .eq(comparator_3_eq));  // open: gt, lt
  assign bitpal = {{31{1'b0}}, or_2_out};  // Bit_Extender bit_extender_6
  Comparator #(.width(32)) comparator_4 (
    .a(A),
    .b({B[0], B[1], B[2], B[3], B[4], B[5], B[6], B[7], B[8], B[9], B[10], B[11], B[12], B[13], B[14], B[15], B[16], B[17], B[18], B[19], B[20], B[21], B[22], B[23], B[24], B[25], B[26], B[27], B[28], B[29], B[30], B[31]}),
    .eq(comparator_4_eq));  // open: gt, lt
  assign sir = {{31{1'b0}}, comparator_4_eq};  // Bit_Extender bit_extender_7

  // Notes on the sheet:
  //   INPUTS to your circuit
  //   DON'T CHANGE THE LOCATIONS OF THE INPUTS AND OUTPUTS!
  //   OUTPUT from your circuit
endmodule
