// Logisim project alu.circ as structural Verilog: 1 circuit, main circuit alu
module alu (
  input  [31:0] A,
  input  [31:0] B,
  input  [3:0] ALUSel,
  output [31:0] Result
);

  wire comparator_1_lt, comparator_2_lt, xor_1_out;
  wire [4:0] bit_extender_1_out, bit_extender_2_out, bit_extender_4_out;
  wire [31:0] add, and1, divu, mulh, mulhu, mult, multiplexer_1_out, multiplexer_2_out, multiplier_1_cout,
       multiplier_1_out, negator_1_out, negator_2_out, negator_3_out, negator_4_out, or1, remu, sll1, slt,
       sltu, sra1, srl1, sub, subtractor_2_out, xor1;

  Multiplexer #(.width(32), .enable("false")) multiplexer_1 (
    .in0(A), .in1(negator_1_out), .out(multiplexer_1_out), .sel(A[31]));
  Negator #(.width(32)) negator_1 (.in(A), .out(negator_1_out));
  Multiplexer #(.width(32), .enable("false")) multiplexer_2 (
    .in0(B), .in1(negator_2_out), .out(multiplexer_2_out), .sel(B[31]));
  Negator #(.width(32)) negator_2 (.in(B), .out(negator_2_out));
  Adder #(.width(32)) adder_1 (.a(A), .b(B), .out(add));  // open: cin, cout
  Subtractor #(.width(32)) subtractor_1 (.a(A), .b(B), .out(sub));  // open: bin, bout
  Multiplier #(.width(32)) multiplier_1 (
    .a(multiplexer_1_out), .b(multiplexer_2_out), .out(multiplier_1_out), .cout(multiplier_1_cout));  // open: cin
  Negator #(.width(32)) negator_3 (.in(multiplier_1_cout), .out(negator_3_out));
  xor xor_1 (xor_1_out, A[31], B[31]);
  Negator #(.width(32)) negator_4 (.in(multiplier_1_out), .out(negator_4_out));
  Subtractor #(.width(32)) subtractor_2 (.a(negator_3_out), .b(32'h1), .out(subtractor_2_out));  // open: bin, bout
  Multiplexer #(.width(32), .enable("false")) multiplexer_3 (
    .in0(multiplier_1_out), .in1(negator_4_out), .out(mult), .sel(xor_1_out));
  Multiplexer #(.width(32), .enable("false")) multiplexer_4 (
    .in0(multiplier_1_cout), .in1(subtractor_2_out), .out(mulh), .sel(xor_1_out));
  Divider #(.width(32)) divider_1 (.a(A), .b(B), .out(divu), .rem(remu));  // open: upper
  assign and1 = A & B;  // AND_Gate and_1, 32 bits wide
  assign or1 = A | B;  // OR_Gate or_1, 32 bits wide
  assign xor1 = A ^ B;  // XOR_Gate xor_2, 32 bits wide
  Bit_Extender #(.in_width(32), .out_width(5)) bit_extender_1 (.in(B), .out(bit_extender_1_out));
  Comparator #(.width(32)) comparator_1 (.a(A), .b(B), .lt(comparator_1_lt));  // open: gt, eq
  Bit_Extender #(.in_width(32), .out_width(5)) bit_extender_2 (.in(B), .out(bit_extender_2_out));
  Multiplexer #(.select(4), .width(32), .enable("false")) multiplexer_5 (
    .in0(add), .in1(sub), .in2(mulh), .in3(mult), .in4(divu), .in5(remu), .in6(and1), .in7(or1), .in8(xor1),
    .in9(sll1), .in10(slt), .in11(sra1), .in12(srl1), .in13(B), .in14(sltu), .in15(mulhu), .out(Result),
    .sel(ALUSel));
  Shifter #(.width(32)) shifter_1 (.in(A), .\dist (bit_extender_1_out), .out(sll1));
  assign slt = {{31{1'b0}}, comparator_1_lt};  // Bit_Extender bit_extender_3
  Shifter #(.width(32), .shift("ar")) shifter_2 (.in(A), .\dist (bit_extender_2_out), .out(sra1));
  Bit_Extender #(.in_width(32), .out_width(5)) bit_extender_4 (.in(B), .out(bit_extender_4_out));
  Comparator #(.width(32), .mode("unsigned")) comparator_2 (.a(A), .b(B), .lt(comparator_2_lt));  // open: gt, eq
  Multiplier #(.width(32)) multiplier_2 (.a(A), .b(B), .cout(mulhu));  // open: out, cin
  Shifter #(.width(32), .shift("lr")) shifter_3 (.in(A), .\dist (bit_extender_4_out), .out(srl1));
  assign sltu = {{31{1'b0}}, comparator_2_lt};  // Bit_Extender bit_extender_5

  // Other names for the same wires on the sheet: bonly[31:0] = B

  // Notes on the sheet:
  //   INPUTS to your circuit
  //   DON'T CHANGE THE LOCATIONS OF THE INPUTS AND OUTPUTS!
  //   OUTPUT from your circuit
endmodule
