// Logisim project cpu.circ as structural Verilog: 5 circuits, main circuit main
module main (
  input  [31:0] INSTRUCTION,
  input  CLOCK,
  output [31:0] FETCH_ADDRESS,
  output [31:0] ra,
  output [31:0] sp,
  output [31:0] t0,
  output [31:0] t1,
  output [31:0] t2,
  output [31:0] s0,
  output [31:0] s1,
  output [31:0] a0
);

  wire ASel, BrEq, BrLt, BRUn, BSel, MemRW, PCSel, RegWEn;
  wire [1:0] WBSel;
  wire [2:0] func3, ImmSel;
  wire [3:0] ALUSel;
  wire [4:0] rd, rs1, rs2;
  wire [6:0] func7, opcode;
  wire [31:0] alu_res, DataA, DataB, DMEM_readdata, Imm, Inst, multiplexer_1_out, multiplexer_2_out,
       multiplexer_3_out, multiplexer_4_out, PC, PC_4, PC_pp, PC_pp_4, shifter_2_out, wb;

  Register #(.width(32)) register_1 (.D(PC_pp), .clk(CLOCK), .Q(PC));  // open: en, clr
  Register #(.width(32)) u_PC (.D(multiplexer_1_out), .clk(CLOCK), .Q(PC_pp));  // open: en, clr
  Multiplexer #(.width(32), .enable("false")) multiplexer_1 (
    .in0(PC_pp_4), .in1(alu_res), .out(multiplexer_1_out), .sel(PCSel));
  Register #(.width(32)) register_2 (.D(multiplexer_2_out), .clk(CLOCK), .Q(Inst));  // open: en, clr
  Multiplexer #(.width(32), .enable("false")) multiplexer_2 (
    .in0(INSTRUCTION), .in1(32'h13), .out(multiplexer_2_out), .sel(PCSel));
  Shifter #(.width(32), .shift("lr")) shifter_1 (.in(PC_pp), .\dist (5'b00010), .out(FETCH_ADDRESS));
  Adder #(.width(32)) adder_1 (.a(PC_pp), .b(32'h4), .out(PC_pp_4));  // open: cin, cout
  Adder #(.width(32)) adder_2 (.a(PC), .b(32'h4), .out(PC_4));  // open: cin, cout
  inst_split inst_split_1 (
    .OpCode(opcode), .rd(rd), .func3(func3), .rs1(rs1), .rs2(rs2), .func7(func7), .Instruction(Inst));
  imm_gen imm_gen_1 (.imm(Imm), .immsel(ImmSel), .inst(Inst));
  branch_comp branch_comp_1 (.equal(BrEq), .input_1(DataA), .less_than(BrLt), .un(BRUn), .input_2(DataB));
  control_logic control_logic_1 (
    .func3(func3), .ASel(ASel), .ImmSel(ImmSel), .ALUSel(ALUSel), .PCSel(PCSel), .func7(func7), .BSel(BSel),
    .BrEq(BrEq), .BrUn(BRUn), .opcode(opcode), .RegWEn(RegWEn), .BrLT(BrLt), .MemRW(MemRW), .WBSel(WBSel));
  Multiplexer #(.width(32), .enable("false")) multiplexer_3 (
    .in0(DataA), .in1(PC), .out(multiplexer_3_out), .sel(ASel));
  Multiplexer #(.width(32), .enable("false")) multiplexer_4 (
    .in0(DataB), .in1(Imm), .out(multiplexer_4_out), .sel(BSel));
  alu Arithmetic_Logic_Unit (.A(multiplexer_3_out), .B(multiplexer_4_out), .ALUSel(ALUSel), .Result(alu_res));
  regfile_main RegFile (
    .s1(s1), .t2(t2), .s0(s0), .a0(a0), .t1(t1), .rd(rd), .RegWEn(RegWEn), .Read_Data_1(DataA), .t0(t0),
    .rs2(rs2), .clk(CLOCK), .Read_Data_2(DataB), .sp(sp), .rs1(rs1), .Write_Data(wb), .ra(ra));
  Shifter #(.width(32), .shift("lr")) shifter_2 (.in(alu_res), .\dist (5'b00010), .out(shifter_2_out));
  mem_main DMEM (.WriteAddr(shifter_2_out), .WriteData(DataB), .ReadData(DMEM_readdata), .MemRW(MemRW), .clk(CLOCK));
  Multiplexer #(.select(2), .width(32), .enable("false")) multiplexer_5 (
    .in0(DMEM_readdata), .in1(alu_res), .in2(PC_4), .out(wb), .sel(WBSel));  // open: in3

  // Other names for the same wires on the sheet: clk = CLOCK; fetch_addr[31:0] = FETCH_ADDRESS

  // Notes on the sheet:
  //   Output
  //   Inputs/Outputs from run.circ. DO NOT MOVE THESE.
  //   Inputs
  //   Inputs/Outputs from run.circ. DO NOT MOVE THESE.
endmodule

module control_logic (
  input  [6:0] opcode,
  input  [2:0] func3,
  input  [6:0] func7,
  input  BrEq,
  input  BrLT,
  output PCSel,
  output [2:0] ImmSel,
  output RegWEn,
  output BrUn,
  output BSel,
  output ASel,
  output [3:0] ALUSel,
  output MemRW,
  output [1:0] WBSel
);

  wire and_2_out, BranchCondMet, func3_0, func3_1, func3_2, func3_3, func3_4, func3_5, func3_6, func3_7,
       func7_00, func7_01, func7_20, IsAUIPC, IsIJType, IsILType, IsIType, IsJAL, IsLUI, IsRType, IsSBType,
       not_2_out, not_3_out, or_1_out, or_2_out, or_5_out, or_7_out;
  wire [1:0] multiplexer_24_out;
  wire [2:0] multiplexer_1_out, multiplexer_2_out, multiplexer_3_out, multiplexer_4_out;
  wire [3:0] ALUSel_I, ALUSel_R, multiplexer_5_out, multiplexer_6_out, multiplexer_8_out, multiplexer_9_out,
       multiplexer_11_out, multiplexer_12_out, multiplexer_13_out, multiplexer_14_out, multiplexer_15_out,
       multiplexer_16_out, multiplexer_17_out, multiplexer_18_out, multiplexer_19_out, multiplexer_20_out,
       multiplexer_21_out, multiplexer_22_out;

  Comparator #(.width(7), .mode("unsigned")) comparator_1 (.a(opcode), .b(7'b0110011), .eq(IsRType));  // open: gt, lt
  Comparator #(.width(7), .mode("unsigned")) comparator_2 (.a(opcode), .b(7'b0000011), .eq(IsILType));  // open: gt, lt
  Comparator #(.width(7), .mode("unsigned")) comparator_3 (.a(opcode), .b(7'b0010011), .eq(IsIType));  // open: gt, lt
  Comparator #(.width(7), .mode("unsigned")) comparator_4 (.a(opcode), .b(7'b0100011), .eq(MemRW));  // open: gt, lt
  Comparator #(.width(7), .mode("unsigned")) comparator_5 (.a(opcode), .b(7'b1100011), .eq(IsSBType));  // open: gt, lt
  Comparator #(.width(7), .mode("unsigned")) comparator_6 (.a(opcode), .b(7'b0010111), .eq(IsAUIPC));  // open: gt, lt
  Comparator #(.width(7), .mode("unsigned")) comparator_7 (.a(opcode), .b(7'b0110111), .eq(IsLUI));  // open: gt, lt
  Comparator #(.width(7), .mode("unsigned")) comparator_8 (.a(opcode), .b(7'b1101111), .eq(IsJAL));  // open: gt, lt
  Comparator #(.width(7), .mode("unsigned")) comparator_9 (.a(opcode), .b(7'b1100111), .eq(IsIJType));  // open: gt, lt
  Comparator #(.width(3), .mode("unsigned")) comparator_10 (.a(func3), .b(3'b000), .eq(func3_0));  // open: gt, lt
  Comparator #(.width(3), .mode("unsigned")) comparator_11 (.a(func3), .b(3'b001), .eq(func3_1));  // open: gt, lt
  Comparator #(.width(3), .mode("unsigned")) comparator_12 (.a(func3), .b(3'b010), .eq(func3_2));  // open: gt, lt
  Comparator #(.width(3), .mode("unsigned")) comparator_13 (.a(func3), .b(3'b011), .eq(func3_3));  // open: gt, lt
  Comparator #(.width(3), .mode("unsigned")) comparator_14 (.a(func3), .b(3'b100), .eq(func3_4));  // open: gt, lt
  Comparator #(.width(3), .mode("unsigned")) comparator_15 (.a(func3), .b(3'b101), .eq(func3_5));  // open: gt, lt
  Comparator #(.width(3), .mode("unsigned")) comparator_16 (.a(func3), .b(3'b110), .eq(func3_6));  // open: gt, lt
  Comparator #(.width(3), .mode("unsigned")) comparator_17 (.a(func3), .b(3'b111), .eq(func3_7));  // open: gt, lt
  Multiplexer #(.width(3), .enable("false")) multiplexer_1 (
    .in0(3'b001), .in1(3'b101), .out(multiplexer_1_out), .sel(IsJAL));
  or or_1 (or_1_out, func3_6, func3_7);
  not not_1 (BSel, IsRType);
  Comparator #(.width(7), .mode("unsigned")) comparator_18 (.a(func7), .b({7{1'b0}}), .eq(func7_00));  // open: gt, lt
  Comparator #(.width(7), .mode("unsigned")) comparator_19 (.a(func7), .b(7'b0000001), .eq(func7_01));  // open: gt, lt
  Comparator #(.width(7), .mode("unsigned")) comparator_20 (.a(func7), .b(7'b0100000), .eq(func7_20));  // open: gt, lt
  Multiplexer #(.width(3), .enable("false")) multiplexer_2 (
    .in0(multiplexer_1_out), .in1(3'b100), .out(multiplexer_2_out), .sel(or_2_out));
  or or_2 (or_2_out, IsAUIPC, IsLUI);
  or or_3 (RegWEn, IsRType, IsILType, IsIType, IsAUIPC, IsLUI, IsJAL, IsIJType);
  and and_1 (BrUn, IsSBType, or_1_out);
  or or_4 (ASel, IsSBType, IsAUIPC, IsJAL);
  Multiplexer #(.width(3), .enable("false")) multiplexer_3 (
    .in0(multiplexer_2_out), .in1(3'b011), .out(multiplexer_3_out), .sel(IsSBType));
  Multiplexer #(.width(3), .enable("false")) multiplexer_4 (
    .in0(multiplexer_3_out), .in1(3'b010), .out(multiplexer_4_out), .sel(MemRW));
  Multiplexer #(.width(4), .enable("false")) multiplexer_5 (
    .in0(4'b1100), .in1(4'b1011), .out(multiplexer_5_out), .sel(func7_20));
  Multiplexer #(.width(4), .enable("false")) multiplexer_6 (
    .in0(4'b1011), .in1(4'b0100), .out(multiplexer_6_out), .sel(func7_01));
  Multiplexer #(.width(3), .enable("false")) multiplexer_7 (
    .in0(multiplexer_4_out), .in1(3'b001), .out(ImmSel), .sel(or_5_out));
  or or_5 (or_5_out, IsILType, IsIType, IsIJType);
  Multiplexer #(.width(4), .enable("false")) multiplexer_8 (
    .in0(4'b0101), .in1(4'b0110), .out(multiplexer_8_out), .sel(func7_00));
  Multiplexer #(.width(4), .enable("false")) multiplexer_9 (
    .in0(multiplexer_6_out), .in1(4'b1100), .out(multiplexer_9_out), .sel(func7_00));
  Multiplexer #(.select(3), .width(4), .enable("false")) multiplexer_10 (
    .in0(4'b0000), .in1(4'b1001), .in2(4'b1010), .in4(4'b1000), .in5(multiplexer_5_out), .in6(4'b0111),
    .in7(4'b0110), .out(ALUSel_I), .sel(func3));  // open: in3
  Multiplexer #(.width(4), .enable("false")) multiplexer_11 (
    .in0(multiplexer_8_out), .in1(4'b0111), .out(multiplexer_11_out), .sel(func3_6));
  Multiplexer #(.width(4), .enable("false")) multiplexer_12 (
    .in0(4'b1111), .in1(4'b1110), .out(multiplexer_12_out), .sel(func7_00));
  Multiplexer #(.width(4), .enable("false")) multiplexer_13 (
    .in0(4'b0000), .in1(4'b1101), .out(multiplexer_13_out), .sel(IsLUI));
  Multiplexer #(.width(4), .enable("false")) multiplexer_14 (
    .in0(multiplexer_11_out), .in1(multiplexer_9_out), .out(multiplexer_14_out), .sel(func3_5));
  Multiplexer #(.width(4), .enable("false")) multiplexer_15 (
    .in0(multiplexer_14_out), .in1(4'b1000), .out(multiplexer_15_out), .sel(func3_4));
  Multiplexer #(.width(4), .enable("false")) multiplexer_16 (
    .in0(4'b0010), .in1(4'b1001), .out(multiplexer_16_out), .sel(func7_00));
  Multiplexer #(.width(4), .enable("false")) multiplexer_17 (
    .in0(4'b0001), .in1(4'b0011), .out(multiplexer_17_out), .sel(func7_01));
  and and_2 (and_2_out, IsSBType, BranchCondMet);
  Multiplexer #(.width(4), .enable("false")) multiplexer_18 (
    .in0(multiplexer_13_out), .in1(ALUSel_I), .out(multiplexer_18_out), .sel(IsIType));
  Multiplexer #(.width(4), .enable("false")) multiplexer_19 (
    .in0(multiplexer_15_out), .in1(multiplexer_12_out), .out(multiplexer_19_out), .sel(func3_3));
  Multiplexer #(.width(4), .enable("false")) multiplexer_20 (
    .in0(multiplexer_19_out), .in1(multiplexer_16_out), .out(multiplexer_20_out), .sel(func3_1));
  Multiplexer #(.width(4), .enable("false")) multiplexer_21 (
    .in0(multiplexer_17_out), .in1(4'b0000), .out(multiplexer_21_out), .sel(func7_00));
  or or_6 (PCSel, and_2_out, IsJAL, IsIJType);
  Multiplexer #(.width(4), .enable("false")) multiplexer_22 (
    .in0(multiplexer_18_out), .in1(4'b0000), .out(multiplexer_22_out), .sel(IsILType));
  Multiplexer #(.width(4), .enable("false")) multiplexer_23 (
    .in0(multiplexer_22_out), .in1(ALUSel_R), .out(ALUSel), .sel(IsRType));
  Multiplexer #(.width(2), .enable("false")) multiplexer_24 (
    .in0(2'b01), .in1(2'b10), .out(multiplexer_24_out), .sel(or_7_out));
  or or_7 (or_7_out, IsJAL, IsIJType);
  not not_2 (not_2_out, BrEq);
  not not_3 (not_3_out, BrLT);
  Multiplexer #(.width(4), .enable("false")) multiplexer_25 (
    .in0(multiplexer_20_out), .in1(multiplexer_21_out), .out(ALUSel_R), .sel(func3_0));
  Multiplexer #(.width(2), .enable("false")) multiplexer_26 (
    .in0(multiplexer_24_out), .in1(2'b00), .out(WBSel), .sel(IsILType));
  Multiplexer #(.select(3), .enable("false")) multiplexer_27 (
    .in0(BrEq), .in1(not_2_out), .in4(BrLT), .in6(BrLT), .in7(not_3_out), .out(BranchCondMet), .sel(func3));  // open: in2, in3, in5

  // Other names for the same wires on the sheet: IsSType = MemRW
endmodule

module inst_split (
  input  [31:0] Instruction,
  output [6:0] OpCode,
  output [4:0] rd,
  output [2:0] func3,
  output [4:0] rs1,
  output [4:0] rs2,
  output [6:0] func7
);


  assign func3 = Instruction[14:12];
  assign func7 = Instruction[31:25];
  assign OpCode = Instruction[6:0];
  assign rd = Instruction[11:7];
  assign rs1 = Instruction[19:15];
  assign rs2 = Instruction[24:20];
endmodule

module imm_gen (
  input  [31:0] inst,
  input  [2:0] immsel,
  output [31:0] imm
);

  wire [31:0] bit_extender_1_out, bit_extender_2_out, bit_extender_3_out, bit_extender_4_out;

  assign bit_extender_1_out = {{20{inst[31]}}, inst[31:20]};  // Bit_Extender bit_extender_1
  assign bit_extender_2_out = {{20{inst[31]}}, {inst[31:25], inst[11:7]}};  // Bit_Extender bit_extender_2
  assign bit_extender_3_out = {{19{inst[31]}}, {inst[31], inst[7], inst[30:25], inst[11:8], 1'b0}};  // Bit_Extender bit_extender_3
  assign bit_extender_4_out = {{11{inst[31]}}, {inst[31], inst[19:12], inst[20], inst[30:21], 1'b0}};  // Bit_Extender bit_extender_4
  Multiplexer #(.select(3), .width(32), .enable("false")) multiplexer_1 (
    .in1(bit_extender_1_out), .in2(bit_extender_2_out), .in3(bit_extender_3_out),
    .in4({inst[31:12], {12{1'b0}}}), .in5(bit_extender_4_out), .out(imm), .sel(immsel));  // open: in0, in6, in7
endmodule

module branch_comp (
  input  [31:0] input_1,
  input  [31:0] input_2,
  input  un,
  output equal,
  output less_than
);

  wire comparator_1_eq, comparator_1_lt, comparator_2_eq, comparator_2_lt;

  Comparator #(.width(32)) comparator_1 (
    .a(input_1), .b(input_2), .eq(comparator_1_eq), .lt(comparator_1_lt));  // open: gt
  Comparator #(.width(32), .mode("unsigned")) comparator_2 (
    .a(input_1), .b(input_2), .eq(comparator_2_eq), .lt(comparator_2_lt));  // open: gt
  Multiplexer #(.enable("false")) multiplexer_1 (.in0(comparator_1_eq), .in1(comparator_2_eq), .out(equal), .sel(un));
  Multiplexer #(.enable("false")) multiplexer_2 (
    .in0(comparator_1_lt), .in1(comparator_2_lt), .out(less_than), .sel(un));
endmodule
