// Logisim project mem.circ as structural Verilog: 1 circuit, main circuit main
module main (
  input  [31:0] WriteAddr,
  input  [31:0] WriteData,
  input  MemRW,
  input  clk,
  output [31:0] ReadData
);

  wire not_1_out;

  RAM #(.addrWidth(14), .dataWidth(32), .trigger("falling"), .databus("bibus")) DataRAM (
    .addr(WriteAddr[13:0]), .we(MemRW), .oe(not_1_out), .clk(clk), .din(WriteData), .dout(ReadData));
  not not_1 (not_1_out, MemRW);
endmodule
