// Logisim project regfile.circ as structural Verilog: 1 circuit, main circuit main
module main (
  input  [4:0] rs1,
  input  [4:0] rs2,
  input  [4:0] rd,
  input  [31:0] Write_Data,
  input  RegWEn,
  input  clk,
  output [31:0] ra,
  output [31:0] sp,
  output [31:0] t0,
  output [31:0] t1,
  output [31:0] t2,
  output [31:0] s0,
  output [31:0] s1,
  output [31:0] a0,
  output [31:0] Read_Data_1,
  output [31:0] Read_Data_2
);

  wire demultiplexer_1_out1, demultiplexer_1_out2, demultiplexer_1_out5, demultiplexer_1_out6,
       demultiplexer_1_out7, demultiplexer_1_out8, demultiplexer_1_out9, demultiplexer_1_out10;
  wire [31:0] undriven, undriven_2, undriven_3, undriven_4, undriven_5, undriven_6, undriven_7, undriven_8,
       undriven_9, undriven_10, undriven_11, undriven_12, undriven_13, undriven_14, undriven_15, undriven_16,
       undriven_17, undriven_18, undriven_19, undriven_20, undriven_21, undriven_22, undriven_23,
       undriven_24, undriven_25, undriven_26, undriven_27, undriven_28, undriven_29, undriven_30,
       undriven_31, undriven_32, undriven_33, undriven_34, undriven_35, undriven_36, undriven_37,
       undriven_38, undriven_39, undriven_40, undriven_41, undriven_42, undriven_43, undriven_44,
       undriven_45, undriven_46;

  Demultiplexer #(.select(5), .enable("false")) demultiplexer_1 (
    .out1(demultiplexer_1_out1), .out2(demultiplexer_1_out2), .out5(demultiplexer_1_out5),
    .out6(demultiplexer_1_out6), .out7(demultiplexer_1_out7), .out8(demultiplexer_1_out8),
    .out9(demultiplexer_1_out9), .out10(demultiplexer_1_out10), .in(RegWEn), .sel(rd));  // open: out0, out3, out4, out11, out12, out13, out14, out15, out16, out17, out18, out19, out20, out21, out22, out23, out24, out25, out26, out27, out28, out29, out30, out31
  Register #(.width(32)) x1 (.D(Write_Data), .en(demultiplexer_1_out1), .clk(clk), .Q(ra));  // open: clr
  Register #(.width(32)) x2 (.D(Write_Data), .en(demultiplexer_1_out2), .clk(clk), .Q(sp));  // open: clr
  Register #(.width(32)) x5 (.D(Write_Data), .en(demultiplexer_1_out5), .clk(clk), .Q(t0));  // open: clr
  Register #(.width(32)) x6 (.D(Write_Data), .en(demultiplexer_1_out6), .clk(clk), .Q(t1));  // open: clr
  Register #(.width(32)) x7 (.D(Write_Data), .en(demultiplexer_1_out7), .clk(clk), .Q(t2));  // open: clr
  Register #(.width(32)) x8 (.D(Write_Data), .en(demultiplexer_1_out8), .clk(clk), .Q(s0));  // open: clr
  Register #(.width(32)) x9 (.D(Write_Data), .en(demultiplexer_1_out9), .clk(clk), .Q(s1));  // open: clr
  Register #(.width(32)) x10 (.D(Write_Data), .en(demultiplexer_1_out10), .clk(clk), .Q(a0));  // open: clr
  Multiplexer #(.select(5), .width(32), .enable("false")) multiplexer_1 (
    .in0({32{1'b0}}), .in1(ra), .in2(sp), .in3(undriven), .in4(undriven_2), .in5(t0), .in6(t1), .in7(t2),
    .in8(s0), .in9(s1), .in10(a0), .in11(undriven_3), .in12(undriven_4), .in13(undriven_5),
    .in14(undriven_6), .in15(undriven_7), .in16(undriven_8), .in17(undriven_9), .in18(undriven_10),
    .in19(undriven_11), .in20(undriven_12), .in21(undriven_13), .in22(undriven_14), .in23(undriven_15),
    .in24(undriven_16), .in25(undriven_17), .in26(undriven_18), .in27(undriven_19), .in28(undriven_20),
    .in29(undriven_21), .in30(undriven_22), .in31(undriven_23), .out(Read_Data_1), .sel(rs1));
  Multiplexer #(.select(5), .width(32), .enable("false")) multiplexer_2 (
    .in0({32{1'b0}}), .in1(ra), .in2(sp), .in3(undriven), .in4(undriven_2), .in5(t0), .in6(t1), .in7(t2),
    .in8(s0), .in9(s1), .in10(a0), .in11(undriven_3), .in12(undriven_4), .in13(undriven_5),
    .in14(undriven_6), .in15(undriven_7), .in16(undriven_8), .in17(undriven_9), .in18(undriven_10),
    .in19(undriven_11), .in20(undriven_12), .in21(undriven_13), .in22(undriven_14), .in23(undriven_15),
    .in24(undriven_16), .in25(undriven_17), .in26(undriven_18), .in27(undriven_19), .in28(undriven_20),
    .in29(undriven_21), .in30(undriven_22), .in31(undriven_23), .out(Read_Data_1), .sel(rs1));
  Multiplexer #(.select(5), .width(32), .enable("false")) multiplexer_3 (
    .in0({32{1'b0}}), .in1(ra), .in2(sp), .in3(undriven_24), .in4(undriven_25), .in5(t0), .in6(t1), .in7(t2),
    .in8(s0), .in9(s1), .in10(a0), .in11(undriven_26), .in12(undriven_27), .in13(undriven_28),
    .in14(undriven_29), .in15(undriven_30), .in16(undriven_31), .in17(undriven_32), .in18(undriven_33),
    .in19(undriven_34), .in20(undriven_35), .in21(undriven_36), .in22(undriven_37), .in23(undriven_38),
    .in24(undriven_39), .in25(undriven_40), .in26(undriven_41), .in27(undriven_42), .in28(undriven_43),
    .in29(undriven_44), .in30(undriven_45), .in31(undriven_46), .out(Read_Data_2), .sel(rs2));
  Multiplexer #(.select(5), .width(32), .enable("false")) multiplexer_4 (
    .in0({32{1'b0}}), .in1(ra), .in2(sp), .in3(undriven_24), .in4(undriven_25), .in5(t0), .in6(t1), .in7(t2),
    .in8(s0), .in9(s1), .in10(a0), .in11(undriven_26), .in12(undriven_27), .in13(undriven_28),
    .in14(undriven_29), .in15(undriven_30), .in16(undriven_31), .in17(undriven_32), .in18(undriven_33),
    .in19(undriven_34), .in20(undriven_35), .in21(undriven_36), .in22(undriven_37), .in23(undriven_38),
    .in24(undriven_39), .in25(undriven_40), .in26(undriven_41), .in27(undriven_42), .in28(undriven_43),
    .in29(undriven_44), .in30(undriven_45), .in31(undriven_46), .out(Read_Data_2), .sel(rs2));

  // Other names for the same wires on the sheet: read_data1[31:0] = Read_Data_1; read_data2[31:0] = Read_Data_2;
  //   read_reg1[4:0] = rs1; read_reg2[4:0] = rs2; write_en = RegWEn; write_reg[4:0] = rd

  // Notes on the sheet:
  //   INPUTS to your circuit
  //   DON'T CHANGE THE LOCATIONS OF THE INPUTS AND OUTPUTS!
  //   These are DEBUG/TEST outputs from your circuit.
  //   OUTPUTS from your circuit
endmodule
